// Logisim project 16-bit ALU.circ as structural Verilog: 3 circuits, main circuit 1-bit ALU
module TEST (
  input  in_1,
  input  [15:0] in_2,
  input  [15:0] in_3,
  input  [1:0] in_4,
  input  [3:0] in_5,
  input  in_6,
  input  in_7,
  output [15:0] out_8,
  output out_9,
  output out_10,
  output out_11
);

  // _16_bits_ALU 16_bits_alu_1: pin names not known; wires that end beside it: in_2, in_3, in_4, in_5, in_6, in_7, in_1, out_8, out_9, out_10, out_11
endmodule

module _1_bit_ALU (
  input  B,
  input  A,
  input  carry_in,
  input  [1:0] Internal_Selector,
  input  Ainvert,
  input  Binvert,
  output result,
  output carry_out
);

  wire adder_1_out, and_1_out, multiplexer_1_out, multiplexer_2_out, not_1_out, not_2_out, or_1_out,
       xor_1_out;

  Multiplexer #(.enable("false")) multiplexer_1 (.in0(A), .in1(not_1_out), .out(multiplexer_1_out), .sel(Ainvert));
  not not_1 (not_1_out, A);
  not not_2 (not_2_out, B);
  Multiplexer #(.enable("false")) multiplexer_2 (.in0(B), .in1(not_2_out), .out(multiplexer_2_out), .sel(Binvert));
  and and_1 (and_1_out, multiplexer_1_out, multiplexer_2_out);
  xor xor_1 (xor_1_out, A, B);
  or or_1 (or_1_out, A, B);
  Adder #(.width(1)) adder_1 (.a(A), .b(multiplexer_2_out), .out(adder_1_out), .cin(carry_in), .cout(carry_out));
  Multiplexer #(.select(2), .enable("false")) multiplexer_3 (
    .in0(and_1_out), .in1(or_1_out), .in2(adder_1_out), .in3(xor_1_out), .out(result), .sel(Internal_Selector));
endmodule

module _16_bits_ALU (
  input  carryin,
  input  [15:0] A,
  input  [15:0] B,
  input  [3:0] External_Selector,
  input  Binvert,
  input  [1:0] Internal_selector,
  input  Ainvert,
  output [15:0] Result,
  output Zero,
  output overflow,
  output carryout
);

  wire comparator_1_eq, comparator_1_gt, comparator_1_lt, comparator_2_eq, comparator_2_lt,
       n1_bit_alu_1_carry_out, n1_bit_alu_2_carry_out, n1_bit_alu_3_carry_out, n1_bit_alu_4_carry_out,
       n1_bit_alu_5_carry_out, n1_bit_alu_6_carry_out, n1_bit_alu_7_carry_out, n1_bit_alu_8_carry_out,
       n1_bit_alu_9_carry_out, n1_bit_alu_10_carry_out, n1_bit_alu_11_carry_out, n1_bit_alu_12_carry_out,
       n1_bit_alu_13_carry_out, n1_bit_alu_14_carry_out, n1_bit_alu_15_carry_out, not_1_out, or_1_out,
       or_2_out;
  wire [15:0] bit_extender_1_out, bit_extender_2_out, bit_extender_3_out, bit_extender_4_out,
       bit_extender_5_out, bit_extender_6_out, bit_extender_7_out, n1_bit_alu_1_result, shifter_1_out,
       shifter_2_out, shifter_3_out, shifter_4_out;

  _1_bit_ALU u_1_bit_alu_1 (
    .result(n1_bit_alu_1_result[0]), .B(B[0]), .A(A[0]), .carry_in(carryin), .Binvert(Binvert),
    .Ainvert(Ainvert), .carry_out(n1_bit_alu_1_carry_out), .Internal_Selector(Internal_selector));
  _1_bit_ALU u_1_bit_alu_2 (
    .result(n1_bit_alu_1_result[1]), .B(B[1]), .A(A[1]), .carry_in(n1_bit_alu_1_carry_out),
    .Binvert(Binvert), .Ainvert(Ainvert), .carry_out(n1_bit_alu_2_carry_out),
    .Internal_Selector(Internal_selector));
  _1_bit_ALU u_1_bit_alu_3 (
    .result(n1_bit_alu_1_result[2]), .B(B[2]), .A(A[2]), .carry_in(n1_bit_alu_2_carry_out),
    .Binvert(Binvert), .Ainvert(Ainvert), .carry_out(n1_bit_alu_3_carry_out),
    .Internal_Selector(Internal_selector));
  _1_bit_ALU u_1_bit_alu_4 (
    .result(n1_bit_alu_1_result[3]), .B(B[3]), .A(A[3]), .carry_in(n1_bit_alu_3_carry_out),
    .Binvert(Binvert), .Ainvert(Ainvert), .carry_out(n1_bit_alu_4_carry_out),
    .Internal_Selector(Internal_selector));
  _1_bit_ALU u_1_bit_alu_5 (
    .result(n1_bit_alu_1_result[4]), .B(B[4]), .A(A[4]), .carry_in(n1_bit_alu_4_carry_out),
    .Binvert(Binvert), .Ainvert(Ainvert), .carry_out(n1_bit_alu_5_carry_out),
    .Internal_Selector(Internal_selector));
  _1_bit_ALU u_1_bit_alu_6 (
    .result(n1_bit_alu_1_result[5]), .B(B[5]), .A(A[5]), .carry_in(n1_bit_alu_5_carry_out),
    .Binvert(Binvert), .Ainvert(Ainvert), .carry_out(n1_bit_alu_6_carry_out),
    .Internal_Selector(Internal_selector));
  _1_bit_ALU u_1_bit_alu_7 (
    .result(n1_bit_alu_1_result[6]), .B(B[6]), .A(A[6]), .carry_in(n1_bit_alu_6_carry_out),
    .Binvert(Binvert), .Ainvert(Ainvert), .carry_out(n1_bit_alu_7_carry_out),
    .Internal_Selector(Internal_selector));
  _1_bit_ALU u_1_bit_alu_8 (
    .result(n1_bit_alu_1_result[7]), .B(B[7]), .A(A[7]), .carry_in(n1_bit_alu_7_carry_out),
    .Binvert(Binvert), .Ainvert(Ainvert), .carry_out(n1_bit_alu_8_carry_out),
    .Internal_Selector(Internal_selector));
  _1_bit_ALU u_1_bit_alu_9 (
    .result(n1_bit_alu_1_result[8]), .B(B[8]), .A(A[8]), .carry_in(n1_bit_alu_8_carry_out),
    .Binvert(Binvert), .Ainvert(Ainvert), .carry_out(n1_bit_alu_9_carry_out),
    .Internal_Selector(Internal_selector));
  _1_bit_ALU u_1_bit_alu_10 (
    .result(n1_bit_alu_1_result[9]), .B(B[9]), .A(A[9]), .carry_in(n1_bit_alu_9_carry_out),
    .Binvert(Binvert), .Ainvert(Ainvert), .carry_out(n1_bit_alu_10_carry_out),
    .Internal_Selector(Internal_selector));
  _1_bit_ALU u_1_bit_alu_11 (
    .result(n1_bit_alu_1_result[10]), .B(B[10]), .A(A[10]), .carry_in(n1_bit_alu_10_carry_out),
    .Binvert(Binvert), .Ainvert(Ainvert), .carry_out(n1_bit_alu_11_carry_out),
    .Internal_Selector(Internal_selector));
  _1_bit_ALU u_1_bit_alu_12 (
    .result(n1_bit_alu_1_result[11]), .B(B[11]), .A(A[11]), .carry_in(n1_bit_alu_11_carry_out),
    .Binvert(Binvert), .Ainvert(Ainvert), .carry_out(n1_bit_alu_12_carry_out),
    .Internal_Selector(Internal_selector));
  _1_bit_ALU u_1_bit_alu_13 (
    .result(n1_bit_alu_1_result[12]), .B(B[12]), .A(A[12]), .carry_in(n1_bit_alu_12_carry_out),
    .Binvert(Binvert), .Ainvert(Ainvert), .carry_out(n1_bit_alu_13_carry_out),
    .Internal_Selector(Internal_selector));
  _1_bit_ALU u_1_bit_alu_14 (
    .result(n1_bit_alu_1_result[13]), .B(B[13]), .A(A[13]), .carry_in(n1_bit_alu_13_carry_out),
    .Binvert(Binvert), .Ainvert(Ainvert), .carry_out(n1_bit_alu_14_carry_out),
    .Internal_Selector(Internal_selector));
  _1_bit_ALU u_1_bit_alu_15 (
    .result(n1_bit_alu_1_result[14]), .B(B[14]), .A(A[14]), .carry_in(n1_bit_alu_14_carry_out),
    .Binvert(Binvert), .Ainvert(Ainvert), .carry_out(n1_bit_alu_15_carry_out),
    .Internal_Selector(Internal_selector));
  _1_bit_ALU u_1_bit_alu_16 (
    .result(n1_bit_alu_1_result[15]), .B(B[15]), .A(A[15]), .carry_in(n1_bit_alu_15_carry_out),
    .Binvert(Binvert), .Ainvert(Ainvert), .carry_out(carryout), .Internal_Selector(Internal_selector));
  xor xor_1 (overflow, n1_bit_alu_15_carry_out, carryout);
  nor nor_1 (Zero, n1_bit_alu_1_result[0], n1_bit_alu_1_result[1], n1_bit_alu_1_result[2], n1_bit_alu_1_result[3], n1_bit_alu_1_result[4], n1_bit_alu_1_result[5], n1_bit_alu_1_result[6], n1_bit_alu_1_result[7], n1_bit_alu_1_result[8], n1_bit_alu_1_result[9], n1_bit_alu_1_result[10], n1_bit_alu_1_result[11], n1_bit_alu_1_result[12], n1_bit_alu_1_result[13], n1_bit_alu_1_result[14], n1_bit_alu_1_result[15]);
  Comparator #(.width(16)) comparator_1 (
    .a(A), .b(B), .gt(comparator_1_gt), .eq(comparator_1_eq), .lt(comparator_1_lt));
  Comparator #(.width(16), .mode("unsigned")) comparator_2 (
    .a(A), .b(B), .eq(comparator_2_eq), .lt(comparator_2_lt));  // open: gt
  not not_1 (not_1_out, comparator_1_eq);
  Shifter #(.width(16)) shifter_1 (.in(A), .\dist (B[3:0]), .out(shifter_1_out));
  Shifter #(.width(16), .shift("lr")) shifter_2 (.in(A), .\dist (B[3:0]), .out(shifter_2_out));
  Shifter #(.width(16), .shift("ar")) shifter_3 (.in(A), .\dist (B[3:0]), .out(shifter_3_out));
  Shifter #(.width(16), .shift("rl")) shifter_4 (.in(A), .\dist (B[3:0]), .out(shifter_4_out));
  assign bit_extender_1_out = {{15{1'b0}}, not_1_out};  // Bit_Extender bit_extender_1
  assign bit_extender_2_out = {{15{1'b0}}, comparator_1_eq};  // Bit_Extender bit_extender_2
  or or_1 (or_1_out, comparator_1_eq, comparator_1_lt);
  or or_2 (or_2_out, comparator_2_eq, comparator_2_lt);
  assign bit_extender_3_out = {{15{1'b0}}, comparator_1_lt};  // Bit_Extender bit_extender_3
  assign bit_extender_4_out = {{15{1'b0}}, or_1_out};  // Bit_Extender bit_extender_4
  assign bit_extender_5_out = {{15{1'b0}}, comparator_2_lt};  // Bit_Extender bit_extender_5
  assign bit_extender_6_out = {{15{1'b0}}, or_2_out};  // Bit_Extender bit_extender_6
  assign bit_extender_7_out = {{15{1'b0}}, comparator_1_gt};  // Bit_Extender bit_extender_7
  Multiplexer #(.select(4), .width(16), .enable("false")) multiplexer_1 (
    .in0(n1_bit_alu_1_result), .in1(shifter_1_out), .in2(shifter_2_out), .in3(shifter_3_out),
    .in4(shifter_4_out), .in5(bit_extender_3_out), .in6(bit_extender_4_out), .in7(bit_extender_5_out),
    .in8(bit_extender_6_out), .in9(bit_extender_7_out), .in14(bit_extender_2_out), .in15(bit_extender_1_out),
    .out(Result), .sel(External_Selector));  // open: in10, in11, in12, in13

  // Other names for the same wires on the sheet: Least_4_bits_of_B[3:0] = B[3:0]
endmodule
