// Logisim project Control Unit.circ as structural Verilog: 15 circuits, main circuit main
// MainControlUnit
module main (
  input  [3:0] OP,
  input  [2:0] FUNCT,
  input  Result,
  output EnablePC,
  output [1:0] PcSrc,
  output LUI,
  output [1:0] RegDst,
  output RegWrite,
  output CarryIn,
  output [1:0] InternalSelector,
  output [3:0] ExternalSelector,
  output Ainvert,
  output [2:0] AluSrc,
  output Binvert,
  output MemWrite,
  output MemRead,
  output MemToReg
);

  enable_pcfin enable_pcfin_1 (
    .op1(OP[2]), .op2(OP[1]), .op3(OP[0]), .fn0(FUNCT[2]), .fn1(FUNCT[1]), .fn2(FUNCT[0]), .res(Result),
    .enablePC(EnablePC), .op0(OP[3]));
  PCsrc pcsrc_1 (
    .op3(OP[3]), .op2(OP[2]), .op1(OP[1]), .op0(OP[0]), .fn2(FUNCT[2]), .fn1(FUNCT[1]), .fn0(FUNCT[0]),
    .PCsrc1(PcSrc[1]), .PCsrc0(PcSrc[0]));
  lui lui_1 (.op3(OP[3]), .op2(OP[2]), .op1(OP[1]), .op0(OP[0]), .lui(LUI));
  regdst regdst_1 (.op3(OP[3]), .op2(OP[2]), .op1(OP[1]), .op0(OP[0]), .regdst1(RegDst[1]), .regdst0(RegDst[0]));
  regwrite regwrite_1 (
    .op3(OP[3]), .op2(OP[2]), .op1(OP[1]), .op0(OP[0]), .fn2(FUNCT[2]), .fn1(FUNCT[1]), .fn0(FUNCT[0]),
    .regwrite(RegWrite));
  carryin carryin_1 (.op3(OP[3]), .fn0(FUNCT[0]), .carryin(CarryIn), .op2(OP[2]), .op1(OP[1]));
  internalSelector internalselector_1 (
    .op3(OP[3]), .op2(OP[2]), .op1(OP[1]), .op0(OP[0]), .fn2(FUNCT[2]), .fn1(FUNCT[1]), .fn0(FUNCT[0]),
    .internal_seector1(InternalSelector[1]), .internal_seector0(InternalSelector[0]));
  external_selector external_selector_1 (
    .op3(OP[3]), .op2(OP[2]), .op1(OP[1]), .op0(OP[0]), .fn2(FUNCT[2]), .fn1(FUNCT[1]), .fn0(FUNCT[0]),
    .ex_s3(ExternalSelector[3]), .ex_s2(ExternalSelector[2]), .ex_s1(ExternalSelector[1]),
    .ex_s0(ExternalSelector[0]));
  A_invert a_invert_1 (.op3(OP[3]), .op2(OP[2]), .op1(OP[1]), .fn1(FUNCT[1]), .A_invert(Ainvert));
  alusrc alusrc_1 (
    .op3(OP[3]), .op2(OP[2]), .op1(OP[1]), .alu_src2(AluSrc[2]), .alu_src1(AluSrc[1]), .alu_src0(AluSrc[0]));
  B_invert b_invert_1 (.op3(OP[3]), .op2(OP[2]), .op1(OP[1]), .fn1(FUNCT[1]), .fn0(FUNCT[0]), .B_invert(Binvert));
  memwrite memwrite_1 (.op3(OP[3]), .op2(OP[2]), .op1(OP[1]), .op0(OP[0]), .memwrite(MemWrite));
  memread memread_1 (.op3(OP[3]), .op2(OP[2]), .op1(OP[1]), .op0(OP[0]), .memread(MemRead));
  mem_to_REG mem_to_reg_1 (.op3(OP[3]), .op2(OP[2]), .op1(OP[1]), .op0(OP[0]), .memtoReg(MemToReg));
endmodule

module enable_pcfin (
  input  op0,
  input  op1,
  input  op2,
  input  op3,
  input  fn0,
  input  fn1,
  input  fn2,
  input  res,
  output enablePC
);

  wire and_1_out, and_2_out, and_3_out, and_4_out, not_1_out, not_2_out, not_3_out, not_4_out;

  not not_1 (not_1_out, op1);
  not not_2 (not_2_out, op2);
  not not_3 (not_3_out, op2);
  not not_4 (not_4_out, op1);
  and and_1 (and_1_out, not_1_out, not_2_out, op3, fn0, fn1);
  and and_2 (and_2_out, op1, not_3_out, res);
  and and_3 (and_3_out, op0, not_4_out, op3);
  and and_4 (and_4_out, op0, op1, res);
  or or_1 (enablePC, and_1_out, and_2_out, and_3_out, and_4_out);
endmodule

module PCsrc (
  input  op3,
  input  op2,
  input  op1,
  input  op0,
  input  fn2,
  input  fn1,
  input  fn0,
  output PCsrc1,
  output PCsrc0
);

  wire and_1_out, and_2_out, not_1_out, not_2_out, not_3_out;

  not not_1 (not_1_out, op3);
  not not_2 (not_2_out, op3);
  not not_3 (not_3_out, fn0);
  and and_1 (and_1_out, not_1_out, fn0);
  and and_2 (and_2_out, not_2_out, not_3_out);
  or or_1 (PCsrc1, and_1_out, op2);
  or or_2 (PCsrc0, and_2_out, op2);
endmodule

module lui (
  input  op3,
  input  op2,
  input  op1,
  input  op0,
  output lui
);

  wire not_1_out, not_2_out;

  not not_1 (not_1_out, op2);
  not not_2 (not_2_out, op0);
  and and_1 (lui, op3, not_1_out, op1, not_2_out);
endmodule

module regdst (
  input  op3,
  input  op2,
  input  op1,
  input  op0,
  output regdst1,
  output regdst0
);

  wire and_2_out, and_3_out, not_1_out, not_2_out;

  and and_1 (regdst1, op3, op1);
  not not_1 (not_1_out, op3);
  and and_2 (and_2_out, not_1_out, op1);
  and and_3 (and_3_out, op3, not_2_out);
  not not_2 (not_2_out, op0);
  or or_1 (regdst0, and_2_out, op2, and_3_out);
endmodule

module regwrite (
  input  op3,
  input  op2,
  input  op1,
  input  op0,
  input  fn2,
  input  fn1,
  input  fn0,
  output regwrite
);

  wire and_1_out, and_2_out, and_3_out, and_4_out, and_5_out, and_6_out, not_1_out, not_2_out, not_3_out,
       not_4_out, not_5_out, not_6_out, not_7_out, not_8_out, not_9_out, not_10_out, not_11_out, not_12_out,
       not_13_out, not_14_out, not_15_out;

  not not_1 (not_1_out, op3);
  not not_2 (not_2_out, op2);
  not not_3 (not_3_out, op1);
  not not_4 (not_4_out, fn2);
  not not_5 (not_5_out, op3);
  not not_6 (not_6_out, op2);
  not not_7 (not_7_out, op1);
  not not_8 (not_8_out, fn1);
  not not_9 (not_9_out, op2);
  not not_10 (not_10_out, op0);
  not not_11 (not_11_out, op3);
  not not_12 (not_12_out, op2);
  not not_13 (not_13_out, op1);
  not not_14 (not_14_out, op3);
  not not_15 (not_15_out, op2);
  and and_1 (and_1_out, not_1_out, not_2_out, not_3_out, not_4_out);
  and and_2 (and_2_out, not_5_out, not_6_out, not_7_out, not_8_out);
  and and_3 (and_3_out, not_9_out, not_10_out);
  and and_4 (and_4_out, not_11_out, not_12_out, not_13_out, fn0);
  and and_5 (and_5_out, not_14_out, op2, op1);
  and and_6 (and_6_out, op3, not_15_out, op1);
  or or_1 (regwrite, and_1_out, and_2_out, and_3_out, and_4_out, and_5_out, and_6_out);
endmodule

module carryin (
  input  op3,
  input  op2,
  input  op1,
  input  fn0,
  output carryin
);

  wire and_1_out, and_2_out, not_1_out, not_2_out, not_3_out;

  not not_1 (not_1_out, op1);
  not not_2 (not_2_out, op3);
  not not_3 (not_3_out, op3);
  and and_1 (and_1_out, not_2_out, not_1_out, fn0);
  and and_2 (and_2_out, not_3_out, op2, fn0);
  or or_1 (carryin, and_1_out, and_2_out);
endmodule

module internalSelector (
  input  op3,
  input  op2,
  input  op1,
  input  op0,
  input  fn2,
  input  fn1,
  input  fn0,
  output internal_seector1,
  output internal_seector0
);

  wire and_1_out, and_2_out, and_3_out, and_4_out, and_5_out, and_6_out, not_1_out, not_2_out, not_3_out,
       not_4_out, not_5_out, not_6_out, not_7_out, not_8_out, not_9_out, not_10_out, not_11_out, not_12_out,
       not_13_out;

  not not_1 (not_1_out, op2);
  not not_2 (not_2_out, fn2);
  not not_3 (not_3_out, op2);
  not not_4 (not_4_out, op2);
  not not_5 (not_5_out, op3);
  not not_6 (not_6_out, op2);
  not not_7 (not_7_out, op1);
  not not_8 (not_8_out, op0);
  not not_9 (not_9_out, fn2);
  not not_10 (not_10_out, op3);
  not not_11 (not_11_out, op1);
  not not_12 (not_12_out, op0);
  not not_13 (not_13_out, fn1);
  and and_1 (and_1_out, not_1_out, not_2_out, fn1, fn0);
  and and_2 (and_2_out, not_3_out, op0);
  and and_3 (and_3_out, not_4_out, op1);
  and and_4 (and_4_out, not_5_out, not_6_out, not_7_out, not_8_out, not_9_out, fn0);
  and and_5 (and_5_out, not_10_out, not_11_out, not_12_out, not_13_out, fn0);
  and and_6 (and_6_out, op2, op0);
  or or_1 (internal_seector1, and_1_out, and_2_out, and_3_out, op3);
  or or_2 (internal_seector0, and_4_out, and_5_out, and_6_out);
endmodule

module external_selector (
  input  op3,
  input  op2,
  input  op1,
  input  op0,
  input  fn2,
  input  fn1,
  input  fn0,
  output ex_s3,
  output ex_s2,
  output ex_s1,
  output ex_s0
);

  wire and_1_out, and_2_out, and_3_out, and_4_out, and_5_out, and_6_out, and_7_out, and_8_out, and_9_out,
       and_10_out, and_11_out, and_12_out, and_13_out, and_14_out, and_15_out, and_16_out, not_1_out,
       not_2_out, not_3_out, not_4_out, not_5_out, not_6_out, not_7_out, not_8_out, not_9_out, not_10_out,
       not_11_out, not_12_out, not_13_out, not_14_out, not_15_out, not_16_out, not_17_out, not_18_out,
       not_19_out, not_20_out, not_21_out, not_22_out, not_23_out, not_24_out, not_25_out, not_26_out,
       not_27_out, not_28_out, not_29_out, not_30_out, not_31_out;

  not not_1 (not_1_out, op3);
  not not_2 (not_2_out, op1);
  not not_3 (not_3_out, op3);
  not not_4 (not_4_out, op1);
  not not_5 (not_5_out, op3);
  not not_6 (not_6_out, op1);
  not not_7 (not_7_out, op1);
  not not_8 (not_8_out, op1);
  not not_9 (not_9_out, fn0);
  not not_10 (not_10_out, op1);
  not not_11 (not_11_out, op3);
  not not_12 (not_12_out, op1);
  not not_13 (not_13_out, op0);
  not not_14 (not_14_out, fn1);
  not not_15 (not_15_out, op3);
  not not_16 (not_16_out, op1);
  not not_17 (not_17_out, fn0);
  not not_18 (not_18_out, op3);
  not not_19 (not_19_out, op1);
  not not_20 (not_20_out, op3);
  not not_21 (not_21_out, op1);
  not not_22 (not_22_out, fn0);
  not not_23 (not_23_out, op3);
  not not_24 (not_24_out, op2);
  not not_25 (not_25_out, op1);
  not not_26 (not_26_out, op0);
  not not_27 (not_27_out, fn0);
  and and_1 (and_1_out, not_1_out, not_2_out, op0, fn2, fn0);
  and and_2 (and_2_out, not_3_out, op2, not_4_out);
  and and_3 (and_3_out, op3, op1);
  and and_4 (and_4_out, not_5_out, not_6_out, fn2, fn1, fn0);
  and and_5 (and_5_out, not_7_out, op0, fn1);
  and and_6 (and_6_out, not_8_out, op0, fn2, not_9_out);
  and and_7 (and_7_out, op2, not_10_out);
  and and_8 (and_8_out, not_11_out, not_12_out, not_13_out, fn2, not_14_out, fn0);
  and and_9 (and_9_out, not_15_out, not_16_out, fn2, fn1, not_17_out);
  and and_10 (and_10_out, not_18_out, not_19_out, op0, fn1, fn0);
  and and_11 (and_11_out, not_20_out, not_21_out, op0, fn2, not_22_out);
  not not_28 (not_28_out, op3);
  and and_12 (and_12_out, not_28_out, op2, not_29_out);
  not not_29 (not_29_out, op1);
  and and_13 (and_13_out, not_23_out, not_24_out, not_25_out, not_26_out, fn2, not_27_out);
  not not_30 (not_30_out, op1);
  and and_14 (and_14_out, not_30_out, op0, fn1);
  not not_31 (not_31_out, op1);
  and and_15 (and_15_out, op2, not_31_out, op0);
  and and_16 (and_16_out, op3, op2);
  or or_1 (ex_s3, and_1_out, and_2_out, and_3_out);
  or or_2 (ex_s2, and_4_out, and_5_out, and_6_out, and_7_out);
  or or_3 (ex_s1, and_8_out, and_9_out, and_10_out, and_11_out, and_12_out);
  or or_4 (ex_s0, and_13_out, and_14_out, and_15_out, and_16_out);
endmodule

module A_invert (
  input  op3,
  input  op2,
  input  op1,
  input  fn1,
  output A_invert
);

  wire not_1_out, not_2_out;

  not not_1 (not_1_out, op3);
  not not_2 (not_2_out, op1);
  and and_1 (A_invert, not_1_out, not_2_out, fn1);
endmodule

module alusrc (
  input  op3,
  input  op2,
  input  op1,
  output alu_src2,
  output alu_src1,
  output alu_src0
);

  wire and_1_out, and_2_out, not_1_out, not_2_out;

  not not_1 (not_1_out, op3);
  and and_1 (and_1_out, not_1_out, op1);
  and and_2 (and_2_out, op3, not_2_out);
  not not_2 (not_2_out, op2);
  or or_1 (alu_src0, and_1_out, and_2_out);

  assign alu_src1 = 1'b0;
  assign alu_src2 = 1'b0;
endmodule

module B_invert (
  input  op3,
  input  op2,
  input  op1,
  input  fn1,
  input  fn0,
  output B_invert
);

  wire and_1_out, and_2_out, not_1_out, not_2_out, not_3_out, not_4_out;

  not not_1 (not_1_out, op3);
  not not_2 (not_2_out, op1);
  not not_3 (not_3_out, op3);
  not not_4 (not_4_out, op1);
  and and_1 (and_1_out, not_1_out, not_2_out, fn0);
  and and_2 (and_2_out, not_3_out, not_4_out, fn1);
  or or_1 (B_invert, and_1_out, and_2_out);
endmodule

module memwrite (
  input  op3,
  input  op2,
  input  op1,
  input  op0,
  output memwrite
);

  wire not_1_out, not_2_out;

  not not_1 (not_1_out, op3);
  not not_2 (not_2_out, op2);
  and and_1 (memwrite, not_1_out, not_2_out, op1, op0);
endmodule

module memread (
  input  op3,
  input  op2,
  input  op1,
  input  op0,
  output memread
);

  wire not_1_out, not_2_out, not_3_out;

  not not_1 (not_1_out, op3);
  not not_2 (not_2_out, op2);
  not not_3 (not_3_out, op0);
  and and_1 (memread, not_1_out, not_2_out, op1, not_3_out);
endmodule

module mem_to_REG (
  input  op3,
  input  op2,
  input  op1,
  input  op0,
  output memtoReg
);

  wire and_1_out, and_2_out, not_1_out, not_2_out;

  not not_1 (not_1_out, op2);
  and and_1 (and_1_out, not_1_out, op1);
  and and_2 (and_2_out, op2, not_2_out);
  not not_2 (not_2_out, op1);
  or or_1 (memtoReg, and_1_out, and_2_out);
endmodule
