// Logisim project PC.circ as structural Verilog: 2 circuits, main circuit PC
module Test (
  input  Clear,
  input  [11:0] INPUT,
  output [15:0] Output
);

  wire [11:0] pc_1_address;

  PC pc_1 (.Input_Enable(Clear), .Input(INPUT), .Address(pc_1_address));  // open: Clear, Clock, Enable
  ROM #(.addrWidth(12), .dataWidth(16)) rom_1 (.addr(pc_1_address), .data(Output));  // open: sel

  // Notes on the sheet:
  //   contents of rom_1 (hex, n*v repeats v):
  //   1111 7*1010
endmodule

module PC (
  input  Input_Enable,
  input  [11:0] Input,
  input  Enable,
  input  Clock,
  input  Clear,
  output [11:0] Address
);

  wire [11:0] adder_1_out, multiplexer_1_out;

  Multiplexer #(.width(12), .enable("false")) multiplexer_1 (
    .in0(adder_1_out), .in1(Input), .out(multiplexer_1_out), .sel(Input_Enable));
  Register #(.width(12)) register_1 (.D(multiplexer_1_out), .en(Enable), .Q(Address), .clk(Clock), .clr(Clear));
  Adder #(.width(12)) adder_1 (.a(Address), .b(12'h1), .out(adder_1_out));  // open: cin, cout
endmodule
