// Logisim project PipeLine Processor.circ as structural Verilog: 12 circuits, main circuit MAIN
module MAIN (
  input  Clear,
  output [11:0] PC,
  output Zero,
  output OverFlow,
  output [15:0] R1,
  output [15:0] R3,
  output [15:0] R5,
  output CarryOut,
  output [15:0] R2,
  output [15:0] R4,
  output [15:0] R6,
  output [15:0] R7
);

  wire Ainvert, Ainvert_1, and_1_out, Binvert, Binvert_1, BranchTaken, CarryIn, CarryIn_1, Clk,
       comparator_1_eq, comparator_2_eq, comparator_3_eq, EnableInputPC, Flush, ForwardA, ForwardB,
       JAL_JALR_2, LUI_2, MemForwardA, MemForwardB, MemToReg_2, not_1_out, Stall, WBForwadA, WBForwadB;
  wire [1:0] M_0, M_1, M_2, PCSrc, RegDst;
  wire [2:0] AluSrc, AluSrc_1, Funct, rd_1, rd_2, rd_3, rd_t, rs_t;
  wire [3:0] WB_0, WB_1, WB_3;
  wire [3:3] WB_2;
  wire [5:0] IMM6_out;
  wire [5:3] IMM6;
  wire [8:3] EX_1;
  wire [11:0] adder_1_out, adder_2_out, adder_3_out, bit_extender_1_out, bit_extender_2_out,
       bit_extender_4_out, EX_0, IMM12_out, IMM12_out_2, InputPc, PC1, PC2, PC3, shifter_1_out;
  wire [11:6] IMM12;
  wire [14:0] Ctrl;
  wire [15:0] ALU_Result_Out, bit_extender_3_out, bit_extender_5_out, Instruction, multiplexer_5_out,
       multiplexer_6_out, multiplexer_7_out, multiplexer_8_out, multiplexer_12_out, multiplexer_13_out,
       multiplexer_14_out, n16_bits_register_file_1_read_data_1, n16_bits_register_file_1_read_data_2,
       R1_content_2, ram_1_data, ReadData1, ReadData1_out, ReadData2, ReadData2_out, ReadData2_out_2, Result,
       rom_1_data, WriteData, WriteDataOut;
  wire [15:12] Instruction_Fetch;

  Clock Clock (.out(Clk));
  not not_1 (not_1_out, Stall);
  PC pc_1 (.Input_Enable(EnableInputPC), .Input(InputPc), .Address(PC), .Clear(Clear), .Clock(Clk), .Enable(not_1_out));
  ROM #(.addrWidth(12), .dataWidth(16)) rom_1 (.addr(PC), .data(rom_1_data), .sel(1'b1));
  Multiplexer #(.width(16), .enable("false")) multiplexer_1 (
    .in0(rom_1_data), .in1({16{1'b0}}), .out(Instruction), .sel(Flush));
  IF_ID if_id_1 (
    .Next_PC(PC), .Instruction_In(Instruction), .Next_PC1(PC1),
    .Instruction_Out({Instruction_Fetch, IMM12, IMM6, Funct}), .Clock(Clk), .Stall(Stall));
  Control_Unit_main main_1 (
    .InternalSelector(Ctrl[14:13]), .OP(Instruction_Fetch), .FUNCT(Funct), .Result(BranchTaken),
    .EnablePC(EnableInputPC), .PcSrc(PCSrc), .LUI(Ctrl[2]), .RegDst(RegDst), .RegWrite(Ctrl[3]),
    .CarryIn(CarryIn), .ExternalSelector(Ctrl[12:9]), .Ainvert(Ainvert), .AluSrc(AluSrc), .Binvert(Binvert),
    .MemWrite(Ctrl[4]), .MemRead(Ctrl[5]), .MemToReg(Ctrl[0]));
  Adder #(.width(12)) adder_1 (.a(PC1), .b(12'h1), .out(adder_1_out));  // open: cin, cout
  assign bit_extender_1_out = {{6{IMM6[5]}}, {IMM6, Funct}};  // Bit_Extender bit_extender_1
  and and_1 (and_1_out, comparator_1_eq, comparator_2_eq);
  Comparator #(.width(4), .mode("unsigned")) comparator_1 (
    .a(4'b0001), .b(Instruction_Fetch), .eq(comparator_1_eq));  // open: gt, lt
  Comparator #(.width(3), .mode("unsigned")) comparator_2 (
    .a(3'b111), .b(Funct), .eq(comparator_2_eq));  // open: gt, lt
  Bit_Extender #(.in_width(16), .out_width(12)) bit_extender_2 (.in(ReadData1), .out(bit_extender_2_out));
  Adder #(.width(12)) adder_2 (.a(adder_1_out), .b(bit_extender_1_out), .out(adder_2_out));  // open: cin, cout
  or or_1 (Ctrl[1], and_1_out, comparator_3_eq);
  Multiplexer #(.select(2), .width(12), .enable("false")) multiplexer_2 (
    .in0({IMM12, IMM6, Funct}), .in1(ReadData1[11:0]), .in2(bit_extender_2_out), .in3(adder_2_out),
    .out(InputPc), .sel(PCSrc));
  Comparator #(.width(4), .mode("unsigned")) comparator_3 (
    .a(4'b1011), .b(Instruction_Fetch), .eq(comparator_3_eq));  // open: gt, lt
  ForwardUnitID_ALU forwardunitid_alu_1 (
    .EX_MEM_Reg_Write(WB_1[3]), .EX_MEM_RD(rd_1), .ID_EX_RS(rs_t), .ID_EX_RT(IMM12[8:6]),
    .ForwardA(ForwardA), .ForwardB(ForwardB));
  ControlHazardsDetection controlhazardsdetection_1 (
    .OP(Instruction_Fetch), .Funct(Funct), .BranchTaken(BranchTaken), .JAL_JALR(Ctrl[1]), .Flush(Flush));
  Multiplexer #(.select(2), .width(3), .enable("false")) multiplexer_3 (
    .in0(IMM6), .in1(IMM12[8:6]), .in2(3'b111), .in3(3'b001), .out(rd_t), .sel(RegDst));
  Multiplexer #(.width(3), .enable("false")) multiplexer_4 (.in0(IMM12[11:9]), .in1(3'b001), .out(rs_t), .sel(Ctrl[2]));
  ForwardFromMemStage forwardfrommemstage_1 (
    .RS(rs_t), .rd_2(rd_2), .RT(IMM12[8:6]), .MemForwardA(MemForwardA), .MemForwardB(MemForwardB),
    .rd_1(rd_1), .RegWrite_2(WB_2[3]));
  ForwardFromWBStage forwardfromwbstage_1 (
    .RS(rs_t), .rd_3(rd_3), .rd_1(rd_1), .RT(IMM12[8:6]), .WBForwardA(WBForwadA), .WBForwardB(WBForwadB),
    .rd_2(rd_2), .RegWrite_3(WB_3[3]));
  _16_Bits_Register_File u_16_bits_register_file_1 (
    .read_register_1(rs_t), .read_register_2(IMM12[8:6]), .Write_Register(rd_3), .WriteData(WriteDataOut),
    .RegWrite(WB_3[3]), .clock(Clk), .read_data_1(n16_bits_register_file_1_read_data_1),
    .read_data_2(n16_bits_register_file_1_read_data_2), .R1(R1), .R2(R2), .R3(R3), .R4(R4), .R5(R5), .R6(R6),
    .R7(R7));
  Multiplexer #(.width(16), .enable("false")) multiplexer_5 (
    .in0(n16_bits_register_file_1_read_data_1), .in1(Result), .out(multiplexer_5_out), .sel(ForwardA));
  Multiplexer #(.width(16), .enable("false")) multiplexer_6 (
    .in0(n16_bits_register_file_1_read_data_2), .in1(Result), .out(multiplexer_6_out), .sel(ForwardB));
  Multiplexer #(.width(16), .enable("false")) multiplexer_7 (
    .in0(multiplexer_5_out), .in1(WriteData), .out(multiplexer_7_out), .sel(MemForwardA));
  Multiplexer #(.width(16), .enable("false")) multiplexer_8 (
    .in0(multiplexer_6_out), .in1(WriteData), .out(multiplexer_8_out), .sel(MemForwardB));
  StallDetectionUnit stalldetectionunit_1 (
    .ForwardA(ForwardA), .ForwardB(ForwardB), .LUI_ID_EX(WB_1[2]), .MemRead_ID_EX(M_1[1]), .Stall(Stall));
  Multiplexer #(.width(18), .enable("false")) multiplexer_9 (
    .in0({AluSrc, Ctrl[14:9], Ainvert, Binvert, CarryIn, Ctrl[5:0]}), .in1({18{1'b0}}),
    .out({EX_0, M_0, WB_0}), .sel(Stall));
  Multiplexer #(.width(16), .enable("false")) multiplexer_10 (
    .in0(multiplexer_7_out), .in1(WriteDataOut), .out(ReadData1), .sel(WBForwadA));
  Multiplexer #(.width(16), .enable("false")) multiplexer_11 (
    .in0(multiplexer_8_out), .in1(WriteDataOut), .out(ReadData2), .sel(WBForwadB));
  Comparator_DecStage comparator_decstage_1 (
    .OP(Instruction_Fetch), .LSB_of_RT(IMM12[6]), .read_data_1(ReadData1), .read_data_2(ReadData2),
    .BranchTaken(BranchTaken));
  ID_EX id_ex_1 (
    .WB(WB_0), .M(M_0), .EX(EX_0), .PC1(PC1), .Read_data1(ReadData1), .Read_data_2(ReadData2),
    .Imm12({IMM12, IMM6, Funct}), .Imm6({IMM6, Funct}), .rd(rd_t), .WB_2(WB_1), .M_2(M_1),
    .EX_2({AluSrc_1, EX_1, Ainvert_1, Binvert_1, CarryIn_1}), .PC2(PC2), .Read_data1_2(ReadData1_out),
    .Read_data_2_2(ReadData2_out), .Imm12_2(IMM12_out), .Imm6_2(IMM6_out), .rd_2(rd_1), .Clock(Clk));
  assign bit_extender_3_out = {{10{IMM6_out[5]}}, IMM6_out};  // Bit_Extender bit_extender_3
  Multiplexer #(.width(16), .enable("false")) multiplexer_12 (
    .in0(ReadData2_out), .in1(bit_extender_3_out), .out(multiplexer_12_out), .sel(AluSrc_1[0]));
  _16_bits_ALU u_16_bits_alu_1 (
    .A(ReadData1_out), .B(multiplexer_12_out), .Binvert(Binvert_1), .Internal_selector(EX_1[8:7]),
    .Ainvert(Ainvert_1), .overflow(OverFlow), .carryout(CarryOut), .carryin(CarryIn_1),
    .External_Selector(EX_1[6:3]), .Result(Result), .Zero(Zero));
  Ex_MEM ex_mem_1 (
    .WB(WB_1), .M(M_1), .PC2(PC2), .ALU_Result(Result), .Read_data_2_out(ReadData2_out), .Imm12(IMM12_out),
    .rd(rd_1), .WB_2({WB_2[3], LUI_2, JAL_JALR_2, MemToReg_2}), .M_2(M_2), .ALU_Result_out(ALU_Result_Out),
    .Mem_Data_In(ReadData2_out_2), .Imm12_2(IMM12_out_2), .rd_2(rd_2), .Clock(Clk),
    .R1_Content_1(ReadData1_out), .R1_Content_2(R1_content_2), .PC3(PC3));
  Bit_Extender #(.in_width(16), .out_width(12)) bit_extender_4 (.in(ALU_Result_Out), .out(bit_extender_4_out));
  Adder #(.width(12)) adder_3 (.a(PC3), .b(12'h1), .out(adder_3_out));  // open: cin, cout
  RAM #(.addrWidth(12), .dataWidth(16), .bus("separate")) ram_1 (
    .addr(bit_extender_4_out), .din(ReadData2_out_2), .data(ram_1_data), .str(M_2[0]), .sel(1'b1), .clk(Clk),
    .ld(M_2[1]));  // open: clr
  Shifter #(.width(12)) shifter_1 (.in(IMM12_out_2), .\dist (4'b0100), .out(shifter_1_out));
  assign bit_extender_5_out = {{4{1'b0}}, adder_3_out};  // Bit_Extender bit_extender_5
  Multiplexer #(.width(16), .enable("false")) multiplexer_13 (
    .in0(ALU_Result_Out), .in1(ram_1_data), .out(multiplexer_13_out), .sel(MemToReg_2));
  Multiplexer #(.width(16), .enable("false")) multiplexer_14 (
    .in0(multiplexer_13_out), .in1(bit_extender_5_out), .out(multiplexer_14_out), .sel(JAL_JALR_2));
  Multiplexer #(.width(16), .enable("false")) multiplexer_15 (
    .in0(multiplexer_14_out), .in1({shifter_1_out, R1_content_2[3:0]}), .out(WriteData), .sel(LUI_2));
  MEM_WB mem_wb_1 (
    .WB({WB_2[3], LUI_2, JAL_JALR_2, MemToReg_2}), .WriteData(WriteData), .rd(rd_2), .WB_2(WB_3),
    .WriteDataOut(WriteDataOut), .rd_2(rd_3), .Clock(Clk));

  // Other names for the same wires on the sheet: MemToReg = Ctrl[0]; WB[3:0] = Ctrl[3:0]; JAL_JALR = Ctrl[1];
  //   LUI = Ctrl[2]; RegWrite = Ctrl[3]; M[1:0] = Ctrl[5:4]; MemWrite_t = Ctrl[4]; MemRead_t = Ctrl[5];
  //   Ctrl (some bits) = {AluSrc, Ainvert, Binvert, CarryIn};
  //   EX[11:0] = {AluSrc, Ctrl[14:9], Ainvert, Binvert, CarryIn}; ExternalSelector[3:0] = Ctrl[12:9];
  //   InternalSelector[1:0] = Ctrl[14:13]; EX_1 (some bits) = {AluSrc_1, Ainvert_1, Binvert_1, CarryIn_1};
  //   ExternalSelector_1[3:0] = EX_1[6:3]; InternalSelector_1[1:0] = EX_1[8:7]; IMM6[2:0] = Funct;
  //   IMM12[5:0] = {IMM6, Funct}; Instruction_Fetch[11:0] = {IMM12, IMM6, Funct}; RD[2:0] = IMM6;
  //   LSB_of_RT = IMM12[6]; RT[2:0] = IMM12[8:6]; RS[2:0] = IMM12[11:9]; OP[3:0] = Instruction_Fetch;
  //   MEMWRITE = M_2[0]; MEMREAD = M_2[1]; WB_2[2:0] = {LUI_2, JAL_JALR_2, MemToReg_2}

  // Notes on the sheet:
  //   contents of rom_1 (hex, n*v repeats v):
  //   a384 8354 35b 2040 2081 20c2 890a 1921 1520 14f2 4182 1290 403b 3100 b012 55c 1b68 403f 4e9 2040
  //   2285 22c6 4e0 3100 1e06
  //   To Forward from ALU Stage
  //   To flush when a BRANCH is taken OR a JUMP is executed.
  //   MEM Forward from MEM Stage
  //   MEM Forward from WB Stage
  //   Stall when LUI OR LW is found in ALU Stage
  //   Comparator_DecStage/Branch Instructions
  //   LUI
endmodule

module _16_Bits_Register_File (
  input  [2:0] read_register_1,
  input  [2:0] read_register_2,
  input  [2:0] Write_Register,
  input  [15:0] WriteData,
  input  RegWrite,
  input  clock,
  output [15:0] R2,
  output [15:0] R1,
  output [15:0] read_data_1,
  output [15:0] read_data_2,
  output [15:0] R6,
  output [15:0] R7,
  output [15:0] R3,
  output [15:0] R4,
  output [15:0] R5
);

  wire and_1_out, and_2_out, and_3_out, and_4_out, and_5_out, and_6_out, and_7_out, decoder_1_out1,
       decoder_1_out2, decoder_1_out3, decoder_1_out4, decoder_1_out5, decoder_1_out6, decoder_1_out7;
  wire [15:0] register_1_q;

  Decoder #(.select(3)) decoder_1 (
    .out1(decoder_1_out1), .out2(decoder_1_out2), .out3(decoder_1_out3), .out4(decoder_1_out4),
    .out5(decoder_1_out5), .out6(decoder_1_out6), .out7(decoder_1_out7), .sel(Write_Register), .en(1'b1));  // open: out0
  and and_1 (and_1_out, decoder_1_out1, RegWrite);
  and and_2 (and_2_out, decoder_1_out2, RegWrite);
  and and_3 (and_3_out, decoder_1_out4, RegWrite);
  and and_4 (and_4_out, decoder_1_out3, RegWrite);
  and and_5 (and_5_out, decoder_1_out5, RegWrite);
  and and_6 (and_6_out, decoder_1_out6, RegWrite);
  and and_7 (and_7_out, decoder_1_out7, RegWrite);
  Register #(.width(16)) register_1 (.D({16{1'b0}}), .en(clock), .Q(register_1_q), .clk(clock), .clr(1'b1));
  Register #(.width(16)) register_2 (.D(WriteData), .en(and_1_out), .Q(R1), .clk(clock), .clr(1'b0));
  Register #(.width(16)) register_3 (.D(WriteData), .en(and_2_out), .Q(R2), .clk(clock), .clr(1'b0));
  Register #(.width(16)) register_4 (.D(WriteData), .en(and_4_out), .Q(R3), .clk(clock), .clr(1'b0));
  Register #(.width(16)) register_5 (.D(WriteData), .en(and_3_out), .Q(R4), .clk(clock), .clr(1'b0));
  Register #(.width(16)) register_6 (.D(WriteData), .en(and_5_out), .Q(R5), .clk(clock), .clr(1'b0));
  Register #(.width(16)) register_7 (.D(WriteData), .en(and_6_out), .Q(R6), .clk(clock), .clr(1'b0));
  Register #(.width(16)) register_8 (.D(WriteData), .en(and_7_out), .Q(R7), .clk(clock), .clr(1'b0));
  Multiplexer #(.select(3), .width(16)) multiplexer_1 (
    .in0(register_1_q), .in1(R1), .in2(R2), .in3(R3), .in4(R4), .in5(R5), .in6(R6), .in7(R7),
    .out(read_data_1), .sel(read_register_1), .en(1'b1));
  Multiplexer #(.select(3), .width(16)) multiplexer_2 (
    .in0(register_1_q), .in1(R1), .in2(R2), .in3(R3), .in4(R4), .in5(R5), .in6(R6), .in7(R7),
    .out(read_data_2), .sel(read_register_2), .en(1'b1));
endmodule

module IF_ID (
  input  [11:0] Next_PC,
  input  [15:0] Instruction_In,
  input  Clock,
  input  Stall,
  output [11:0] Next_PC1,
  output [15:0] Instruction_Out
);

  wire not_1_out;

  not not_1 (not_1_out, Stall);
  Register #(.width(12)) register_1 (.D(Next_PC), .en(not_1_out), .Q(Next_PC1), .clk(Clock));  // open: clr
  Register #(.width(16)) register_2 (
    .D(Instruction_In), .en(not_1_out), .Q(Instruction_Out), .clk(Clock));  // open: clr
endmodule

module ID_EX (
  input  [3:0] WB,
  input  [1:0] M,
  input  [11:0] EX,
  input  [11:0] PC1,
  input  [15:0] Read_data1,
  input  [15:0] Read_data_2,
  input  [11:0] Imm12,
  input  [5:0] Imm6,
  input  [2:0] rd,
  input  Clock,
  output [3:0] WB_2,
  output [1:0] M_2,
  output [11:0] EX_2,
  output [11:0] PC2,
  output [15:0] Read_data1_2,
  output [15:0] Read_data_2_2,
  output [11:0] Imm12_2,
  output [5:0] Imm6_2,
  output [2:0] rd_2
);

  Register #(.width(4)) register_1 (.D(WB), .en(1'b1), .Q(WB_2), .clk(Clock));  // open: clr
  Register #(.width(2)) register_2 (.D(M), .en(1'b1), .Q(M_2), .clk(Clock));  // open: clr
  Register #(.width(12)) register_3 (.D(EX), .en(1'b1), .Q(EX_2), .clk(Clock));  // open: clr
  Register #(.width(12)) register_4 (.D(PC1), .en(1'b1), .Q(PC2), .clk(Clock));  // open: clr
  Register #(.width(16)) register_5 (.D(Read_data1), .en(1'b1), .Q(Read_data1_2), .clk(Clock));  // open: clr
  Register #(.width(16)) register_6 (.D(Read_data_2), .en(1'b1), .Q(Read_data_2_2), .clk(Clock));  // open: clr
  Register #(.width(12)) register_7 (.D(Imm12), .en(1'b1), .Q(Imm12_2), .clk(Clock));  // open: clr
  Register #(.width(6)) register_8 (.D(Imm6), .en(1'b1), .Q(Imm6_2), .clk(Clock));  // open: clr
  Register #(.width(3)) register_9 (.D(rd), .en(1'b1), .Q(rd_2), .clk(Clock));  // open: clr
endmodule

// EX/MEM
module Ex_MEM (
  input  [3:0] WB,
  input  [1:0] M,
  input  [11:0] PC2,
  input  [15:0] ALU_Result,
  input  [15:0] R1_Content_1,
  input  [15:0] Read_data_2_out,
  input  [11:0] Imm12,
  input  [2:0] rd,
  input  Clock,
  output [3:0] WB_2,
  output [1:0] M_2,
  output [11:0] PC3,
  output [15:0] ALU_Result_out,
  output [15:0] R1_Content_2,
  output [15:0] Mem_Data_In,
  output [11:0] Imm12_2,
  output [2:0] rd_2
);

  Register #(.width(4)) register_1 (.D(WB), .en(1'b1), .Q(WB_2), .clk(Clock));  // open: clr
  Register #(.width(2)) register_2 (.D(M), .en(1'b1), .Q(M_2), .clk(Clock));  // open: clr
  Register #(.width(12)) register_3 (.D(PC2), .en(1'b1), .Q(PC3), .clk(Clock));  // open: clr
  Register #(.width(16)) register_4 (.D(ALU_Result), .en(1'b1), .Q(ALU_Result_out), .clk(Clock));  // open: clr
  Register #(.width(16)) register_5 (.D(R1_Content_1), .en(1'b1), .Q(R1_Content_2), .clk(Clock));  // open: clr
  Register #(.width(16)) register_6 (.D(Read_data_2_out), .en(1'b1), .Q(Mem_Data_In), .clk(Clock));  // open: clr
  Register #(.width(12)) register_7 (.D(Imm12), .en(1'b1), .Q(Imm12_2), .clk(Clock));  // open: clr
  Register #(.width(3)) register_8 (.D(rd), .en(1'b1), .Q(rd_2), .clk(Clock));  // open: clr
endmodule

module MEM_WB (
  input  [3:0] WB,
  input  [15:0] WriteData,
  input  [2:0] rd,
  input  Clock,
  output [3:0] WB_2,
  output [15:0] WriteDataOut,
  output [2:0] rd_2
);

  Register #(.width(4)) register_1 (.D(WB), .en(1'b1), .Q(WB_2), .clk(Clock));  // open: clr
  Register #(.width(16)) register_2 (.D(WriteData), .en(1'b1), .Q(WriteDataOut), .clk(Clock));  // open: clr
  Register #(.width(3)) register_3 (.D(rd), .en(1'b1), .Q(rd_2), .clk(Clock));  // open: clr
endmodule

module Comparator_DecStage (
  input  [3:0] OP,
  input  LSB_of_RT,
  input  [15:0] read_data_1,
  input  [15:0] read_data_2,
  output BranchTaken
);

  wire BEQ_out, BGEZ_out, BGT_out, BGTZ_out, BLEZ_out, BLT_out, BLTZ_out, BNE_out, comparator_1_eq,
       comparator_1_gt, comparator_1_lt, comparator_2_eq, comparator_2_gt, comparator_2_lt, not_1_out,
       or_1_out, or_2_out;

  Comparator #(.width(16)) comparator_1 (
    .a(read_data_1), .b(read_data_2), .gt(comparator_1_gt), .eq(comparator_1_eq), .lt(comparator_1_lt));
  Comparator #(.width(16)) comparator_2 (
    .a(read_data_1), .b({16{1'b0}}), .gt(comparator_2_gt), .eq(comparator_2_eq), .lt(comparator_2_lt));
  or or_1 (or_1_out, comparator_2_gt, comparator_2_eq);
  or or_2 (or_2_out, comparator_2_eq, comparator_2_lt);
  and BEQ (BEQ_out, ~OP[3], OP[2], ~OP[1], ~OP[0], comparator_1_eq);  // AND_Gate
  not not_1 (not_1_out, comparator_1_eq);
  and BNE (BNE_out, ~OP[3], OP[2], ~OP[1], OP[0], not_1_out);  // AND_Gate
  and BLT (BLT_out, OP[3], OP[2], ~OP[1], OP[0], comparator_1_lt);  // AND_Gate
  or or_3 (BranchTaken, BEQ_out, BNE_out, BLT_out, BGT_out, BLTZ_out, BLEZ_out, BGTZ_out, BGEZ_out);
  and BGT (BGT_out, OP[3], OP[2], OP[1], OP[0], comparator_1_gt);
  and BLTZ (BLTZ_out, OP[3], OP[2], ~OP[1], ~OP[0], comparator_2_lt, ~LSB_of_RT);  // AND_Gate
  and BLEZ (BLEZ_out, OP[3], OP[2], ~OP[1], ~OP[0], or_2_out, LSB_of_RT);  // AND_Gate
  and BGTZ (BGTZ_out, OP[3], OP[2], OP[1], ~OP[0], comparator_2_gt, ~LSB_of_RT);  // AND_Gate
  and BGEZ (BGEZ_out, OP[3], OP[2], OP[1], ~OP[0], or_1_out, LSB_of_RT);  // AND_Gate
endmodule

module ForwardUnitID_ALU (
  input  EX_MEM_Reg_Write,
  input  [2:0] EX_MEM_RD,
  input  [2:0] ID_EX_RS,
  input  [2:0] ID_EX_RT,
  output ForwardA,
  output ForwardB
);

  wire comparator_1_eq, comparator_2_eq, or_1_out;

  or or_1 (or_1_out, EX_MEM_RD[0], EX_MEM_RD[1], EX_MEM_RD[2]);
  Comparator #(.width(3)) comparator_1 (.a(EX_MEM_RD), .b(ID_EX_RS), .eq(comparator_1_eq));  // open: gt, lt
  Comparator #(.width(3)) comparator_2 (.a(EX_MEM_RD), .b(ID_EX_RT), .eq(comparator_2_eq));  // open: gt, lt
  and and_1 (ForwardA, EX_MEM_Reg_Write, comparator_1_eq, or_1_out);
  and and_2 (ForwardB, EX_MEM_Reg_Write, comparator_2_eq, or_1_out);
endmodule

// ControlHazardsDetectionUnit
module ControlHazardsDetection (
  input  [3:0] OP,
  input  [2:0] Funct,
  input  BranchTaken,
  input  JAL_JALR,
  output Flush
);

  wire comparator_1_eq, comparator_2_eq, comparator_3_eq, JR_out;

  Comparator #(.width(4)) comparator_1 (.a(OP), .b(4'b0001), .eq(comparator_1_eq));  // open: gt, lt
  Comparator #(.width(3)) comparator_2 (.a(Funct), .b(3'b110), .eq(comparator_2_eq));  // open: gt, lt
  Comparator #(.width(4)) comparator_3 (.a(OP), .b(4'b1001), .eq(comparator_3_eq));  // open: gt, lt
  and JR (JR_out, comparator_1_eq, comparator_2_eq);
  or or_1 (Flush, JR_out, comparator_3_eq, BranchTaken, JAL_JALR);

  // Notes on the sheet:
  //   Jump
endmodule

module StallDetectionUnit (
  input  ForwardA,
  input  ForwardB,
  input  LUI_ID_EX,
  input  MemRead_ID_EX,
  output Stall
);

  wire or_1_out, or_2_out;

  or or_1 (or_1_out, ForwardA, ForwardB);
  or or_2 (or_2_out, LUI_ID_EX, MemRead_ID_EX);
  and and_1 (Stall, or_1_out, or_2_out);

  // Notes on the sheet:
  //   To check for LUI instruction
  //   To check for LW instruction
endmodule

module ForwardFromMemStage (
  input  [2:0] RS,
  input  [2:0] rd_2,
  input  [2:0] rd_1,
  input  RegWrite_2,
  input  [2:0] RT,
  output MemForwardA,
  output MemForwardB
);

  wire comparator_1_eq, comparator_2_eq, comparator_3_eq, comparator_4_eq, not_1_out, not_2_out, or_1_out;

  Comparator #(.width(3)) comparator_1 (.a(RS), .b(rd_1), .eq(comparator_1_eq));  // open: gt, lt
  Comparator #(.width(3)) comparator_2 (.a(rd_1), .b(RT), .eq(comparator_2_eq));  // open: gt, lt
  Comparator #(.width(3)) comparator_3 (.a(RS), .b(rd_2), .eq(comparator_3_eq));  // open: gt, lt
  or or_1 (or_1_out, rd_2[0], rd_2[1], rd_2[2]);
  not not_1 (not_1_out, comparator_1_eq);
  not not_2 (not_2_out, comparator_2_eq);
  Comparator #(.width(3)) comparator_4 (.a(rd_2), .b(RT), .eq(comparator_4_eq));  // open: gt, lt
  and and_1 (MemForwardA, comparator_3_eq, or_1_out, not_1_out, RegWrite_2);
  and and_2 (MemForwardB, RegWrite_2, or_1_out, not_2_out, comparator_4_eq);
endmodule

module ForwardFromWBStage (
  input  [2:0] rd_2,
  input  [2:0] RS,
  input  [2:0] rd_3,
  input  [2:0] rd_1,
  input  RegWrite_3,
  input  [2:0] RT,
  output WBForwardA,
  output WBForwardB
);

  wire comparator_1_eq, comparator_2_eq, comparator_3_eq, comparator_4_eq, comparator_5_eq, comparator_6_eq,
       not_1_out, not_2_out, not_3_out, not_4_out, or_1_out;

  or or_1 (or_1_out, rd_3[0], rd_3[1], rd_3[2]);
  Comparator #(.width(3)) comparator_1 (.a(RS), .b(rd_3), .eq(comparator_1_eq));  // open: gt, lt
  Comparator #(.width(3)) comparator_2 (.a(RS), .b(rd_1), .eq(comparator_2_eq));  // open: gt, lt
  Comparator #(.width(3)) comparator_3 (.a(rd_2), .b(RT), .eq(comparator_3_eq));  // open: gt, lt
  Comparator #(.width(3)) comparator_4 (.a(rd_1), .b(RT), .eq(comparator_4_eq));  // open: gt, lt
  Comparator #(.width(3)) comparator_5 (.a(rd_3), .b(RT), .eq(comparator_5_eq));  // open: gt, lt
  Comparator #(.width(3)) comparator_6 (.a(rd_2), .b(RS), .eq(comparator_6_eq));  // open: gt, lt
  not not_1 (not_1_out, comparator_2_eq);
  not not_2 (not_2_out, comparator_3_eq);
  not not_3 (not_3_out, comparator_4_eq);
  not not_4 (not_4_out, comparator_6_eq);
  and and_1 (WBForwardB, not_2_out, RegWrite_3, not_3_out, or_1_out, comparator_5_eq);
  and and_2 (WBForwardA, comparator_1_eq, not_4_out, not_1_out, RegWrite_3, or_1_out);
endmodule
